# Fritzing sketch TempHum (saved by Fritzing 0.9.3b)
perfboards: 1

parts:
  Grove1 = Grove OLED 128x96  # not connected
  Raspberry_Pi_Zero1 = Raspberry Pi Zero  # not connected
  S1 = Round Pushbutton  # not connected
  U1 = TEMPERATURE-SENSOR [package=to-92]  # not connected
  S2 = Pushbutton [package="[THT]"]
  RHT1 = Humidity and Temperature Sensor RHT03  # not connected
  VCC1 = Battery  # not connected
  LED1 = LED - 3mm [color="Red (633nm)" package="3 mm [THT]"]  # not connected
  X1 = USB Connectors [package=usb-microb]  # not connected
  U5 = Mini-USB _B_ connector with 5th pin broken out. [package=usb-minib]  # not connected
  R1 = Resistor [tolerance=±5% resistance=220 package=THT]  # not connected
  R2 = Resistor [tolerance=±5% resistance=220 package=THT]  # not connected
  R3 = Resistor [tolerance=±5% resistance=220 package=THT]
  R4 = Resistor [tolerance=±5% resistance=220 package=THT]
  J2 = shrouded pin header, 40 pins [form="♂ (shrouded male)"]  # not connected

nets:
  N1: S2.Pin_1, S2.Pin_2
  N2: S2.Pin_3, S2.Pin_4
  N3: R3.Pin_1, R4.Pin_1
